// Logisim project cpu.circ as structural Verilog: 9 circuits, main circuit main
module main (
  input  RST,
  input  zx,
  input  nx,
  input  [15:0] x,
  input  [15:0] y,
  input  zy,
  input  ny,
  input  f,
  input  no,
  output zr,
  output ng,
  output [15:0] out
);

  wire MAIN_CLK_out, or16way_1_or, undriven_3, undriven_4, undriven_5, undriven_6;
  wire [7:0] undriven, undriven_2;
  wire [14:0] and_2_out;
  wire [15:0] add16_1_sum, and_1_out, multiplexer_1_out, multiplexer_2_out, multiplexer_3_out,
       multiplexer_4_out, multiplexer_5_out, not_1_out, not_2_out, not_3_out;

  Clock MAIN_CLK (.out(MAIN_CLK_out));
  Register RegA ();  // open: D, en, Q, clk, clr
  Register RegA_2 (.en(undriven_5), .clk(undriven_6));  // open: D, Q, clr
  Register RegIns (.D(undriven), .en(undriven_4), .clk(MAIN_CLK_out), .clr(RST));  // open: Q
  Register RegPC (.D(undriven_2), .en(undriven_3), .clk(MAIN_CLK_out), .clr(RST));  // open: Q
  Multiplexer #(.width(16), .enable("false")) multiplexer_1 (
    .in0(x), .in1({16{1'b0}}), .out(multiplexer_1_out), .sel(zx));
  assign not_1_out = ~multiplexer_1_out;  // NOT_Gate not_1, 16 bits wide
  Multiplexer #(.width(16), .enable("false")) multiplexer_2 (
    .in0(y), .in1({16{1'b0}}), .out(multiplexer_2_out), .sel(zy));
  assign not_2_out = ~multiplexer_2_out;  // NOT_Gate not_2, 16 bits wide
  Multiplexer #(.width(16), .enable("false")) multiplexer_3 (
    .in0(x), .in1(not_1_out), .out(multiplexer_3_out), .sel(nx));
  Multiplexer #(.width(16), .enable("false")) multiplexer_4 (
    .in0(y), .in1(not_2_out), .out(multiplexer_4_out), .sel(ny));
  assign and_1_out = multiplexer_3_out & multiplexer_4_out;  // AND_Gate and_1, 16 bits wide
  Add16 add16_1 (.B(multiplexer_4_out), .A(multiplexer_3_out), .Sum(add16_1_sum));  // open: Carry
  Multiplexer #(.width(16), .enable("false")) multiplexer_5 (
    .in0(and_1_out), .in1(add16_1_sum), .out(multiplexer_5_out), .sel(f));
  assign not_3_out = ~multiplexer_5_out;  // NOT_Gate not_3, 16 bits wide
  Multiplexer #(.width(16), .enable("false")) multiplexer_6 (
    .in0(not_3_out), .in1(multiplexer_5_out), .out(out), .sel(no));
  Or16Way or16way_1 (.A(out), .Or(or16way_1_or));
  assign {ng, and_2_out} = out & {16{1'b1}};  // AND_Gate and_2, 16 bits wide
  not not_4 (zr, or16way_1_or);
endmodule

module FA (
  input  a,
  input  b,
  input  c,
  output sum,
  output carry
);

  wire ha_1_carry, ha_1_sum, ha_2_carry;

  HA ha_1 (.A(a), .B(b), .Sum(ha_1_sum), .Carry(ha_1_carry));
  HA ha_2 (.A(ha_1_sum), .B(c), .Sum(carry), .Carry(ha_2_carry));
  or or_1 (sum, ha_1_carry, ha_2_carry);
endmodule

module HA (
  input  A,
  input  B,
  output Sum,
  output Carry
);

  xor xor_1 (Sum, A, B);
  and and_1 (Carry, A, B);
endmodule

module Or16Way (
  input  [15:0] A,
  output Or
);

  wire or_1_out, or_2_out, or_3_out, or_4_out, or_5_out, or_6_out, or_7_out, or_8_out, or_9_out, or_10_out,
       or_11_out, or_12_out, or_13_out, or_14_out;

  or or_1 (or_1_out, A[0], A[1]);
  or or_2 (or_2_out, or_1_out, A[2]);
  or or_3 (or_3_out, or_2_out, A[3]);
  or or_4 (or_4_out, or_3_out, A[4]);
  or or_5 (or_5_out, or_4_out, A[5]);
  or or_6 (or_6_out, or_5_out, A[6]);
  or or_7 (or_7_out, or_6_out, A[7]);
  or or_8 (or_8_out, or_7_out, A[8]);
  or or_9 (or_9_out, or_8_out, A[9]);
  or or_10 (or_10_out, or_9_out, A[10]);
  or or_11 (or_11_out, or_10_out, A[11]);
  or or_12 (or_12_out, or_11_out, A[12]);
  or or_13 (or_13_out, or_12_out, A[13]);
  or or_14 (or_14_out, or_13_out, A[14]);
  or or_15 (Or, or_14_out, A[15]);
endmodule

module Add16 (
  input  [15:0] B,
  input  [15:0] A,
  output Carry,
  output [15:0] Sum
);

  wire and_1_out, and_2_out, and_3_out, and_4_out, and_5_out, and_6_out, and_7_out, and_8_out, and_9_out,
       and_10_out, and_11_out, and_12_out, and_13_out, and_14_out, and_15_out, and_16_out, ha_1_carry,
       ha_1_sum, ha_2_carry, ha_2_sum, ha_3_carry, ha_3_sum, ha_4_carry, ha_4_sum, ha_5_sum, ha_6_sum,
       ha_7_carry, ha_7_sum, ha_8_carry, ha_8_sum, ha_9_carry, ha_9_sum, ha_10_carry, ha_10_sum, ha_11_carry,
       ha_11_sum, ha_12_carry, ha_12_sum, ha_13_carry, ha_13_sum, ha_14_carry, ha_14_sum, ha_15_carry,
       ha_15_sum, ha_16_carry, ha_16_sum, or_2_out, or_3_out, or_4_out, or_5_out, or_6_out, or_7_out,
       or_8_out, or_9_out, or_10_out, or_11_out, or_12_out, or_13_out, or_14_out, or_15_out, or_16_out;

  HA ha_1 (.A(A[15]), .B(B[15]), .Sum(ha_1_sum), .Carry(ha_1_carry));
  and and_1 (and_1_out, ha_1_sum, or_3_out);
  or or_1 (Carry, ha_1_carry, and_1_out);
  xor xor_1 (Sum[15], ha_1_sum, or_3_out);
  HA ha_2 (.A(A[13]), .B(B[13]), .Sum(ha_2_sum), .Carry(ha_2_carry));
  HA ha_3 (.A(A[14]), .B(B[14]), .Sum(ha_3_sum), .Carry(ha_3_carry));
  and and_2 (and_2_out, ha_2_sum, or_4_out);
  or or_2 (or_2_out, ha_2_carry, and_2_out);
  and and_3 (and_3_out, ha_3_sum, or_2_out);
  or or_3 (or_3_out, ha_3_carry, and_3_out);
  xor xor_2 (Sum[14], ha_3_sum, or_2_out);
  HA ha_4 (.A(A[12]), .B(B[12]), .Sum(ha_4_sum), .Carry(ha_4_carry));
  and and_4 (and_4_out, ha_4_sum, or_6_out);
  or or_4 (or_4_out, ha_4_carry, and_4_out);
  xor xor_3 (Sum[13], ha_2_sum, or_4_out);
  HA ha_5 (.A(A[11]), .B(B[11]), .Sum(ha_5_sum), .Carry(ha_5_sum));
  xor xor_4 (Sum[12], ha_4_sum, or_6_out);
  HA ha_6 (.A(A[10]), .B(B[10]), .Sum(ha_6_sum), .Carry(ha_6_sum));
  and and_5 (and_5_out, ha_6_sum, or_8_out);
  or or_5 (or_5_out, ha_6_sum, and_5_out);
  and and_6 (and_6_out, ha_5_sum, or_5_out);
  or or_6 (or_6_out, ha_5_sum, and_6_out);
  xor xor_5 (Sum[11], ha_5_sum, or_5_out);
  HA ha_7 (.A(A[8]), .B(B[8]), .Sum(ha_7_sum), .Carry(ha_7_carry));
  HA ha_8 (.A(A[9]), .B(B[9]), .Sum(ha_8_sum), .Carry(ha_8_carry));
  or or_7 (or_7_out, ha_7_carry, and_8_out);
  and and_7 (and_7_out, ha_8_sum, or_7_out);
  or or_8 (or_8_out, ha_8_carry, and_7_out);
  xor xor_6 (Sum[9], ha_8_sum, or_7_out);
  xor xor_7 (Sum[10], ha_6_sum, or_8_out);
  and and_8 (and_8_out, ha_7_sum, or_9_out);
  xor xor_8 (Sum[8], ha_7_sum, or_9_out);
  HA ha_9 (.A(A[6]), .B(B[6]), .Sum(ha_9_sum), .Carry(ha_9_carry));
  HA ha_10 (.A(A[7]), .B(B[7]), .Sum(ha_10_sum), .Carry(ha_10_carry));
  and and_9 (and_9_out, ha_10_sum, or_11_out);
  or or_9 (or_9_out, ha_10_carry, and_9_out);
  HA ha_11 (.A(A[5]), .B(B[5]), .Sum(ha_11_sum), .Carry(ha_11_carry));
  and and_10 (and_10_out, ha_11_sum, or_12_out);
  or or_10 (or_10_out, ha_11_carry, and_10_out);
  and and_11 (and_11_out, ha_9_sum, or_10_out);
  or or_11 (or_11_out, ha_9_carry, and_11_out);
  xor xor_9 (Sum[6], ha_9_sum, or_10_out);
  xor xor_10 (Sum[7], ha_10_sum, or_11_out);
  HA ha_12 (.A(A[4]), .B(B[4]), .Sum(ha_12_sum), .Carry(ha_12_carry));
  and and_12 (and_12_out, ha_12_sum, or_14_out);
  or or_12 (or_12_out, ha_12_carry, and_12_out);
  xor xor_11 (Sum[5], ha_11_sum, or_12_out);
  xor xor_12 (Sum[4], ha_12_sum, or_14_out);
  HA ha_13 (.A(A[2]), .B(B[2]), .Sum(ha_13_sum), .Carry(ha_13_carry));
  HA ha_14 (.A(A[3]), .B(B[3]), .Sum(ha_14_sum), .Carry(ha_14_carry));
  or or_13 (or_13_out, ha_13_carry, and_15_out);
  and and_13 (and_13_out, ha_14_sum, or_13_out);
  or or_14 (or_14_out, ha_14_carry, and_13_out);
  HA ha_15 (.A(A[1]), .B(B[1]), .Sum(ha_15_sum), .Carry(ha_15_carry));
  and and_14 (and_14_out, ha_15_sum, or_16_out);
  or or_15 (or_15_out, ha_15_carry, and_14_out);
  and and_15 (and_15_out, ha_13_sum, or_15_out);
  xor xor_13 (Sum[2], ha_13_sum, or_15_out);
  xor xor_14 (Sum[3], ha_14_sum, or_13_out);
  HA ha_16 (.A(A[0]), .B(B[0]), .Sum(ha_16_sum), .Carry(ha_16_carry));
  and and_16 (and_16_out, ha_16_sum, 1'b0);
  or or_16 (or_16_out, ha_16_carry, and_16_out);
  xor xor_15 (Sum[1], ha_15_sum, or_16_out);
  xor xor_16 (Sum[0], ha_16_sum, 1'b0);
endmodule

module Inc16 (
  input  [15:0] In,
  output [15:0] out
);

  Add16 add16_1 (.B(In), .A(16'h1), .Sum(out));  // open: Carry
endmodule

// out
module ALU (
  input  zx,
  input  nx,
  input  [15:0] x,
  input  [15:0] y,
  input  zy,
  input  ny,
  input  f,
  input  no,
  output zr,
  output ng,
  output [15:0] out
);

  wire or16way_1_or;
  wire [14:0] and_2_out;
  wire [15:0] add16_1_sum, and_1_out, multiplexer_1_out, multiplexer_2_out, multiplexer_3_out,
       multiplexer_4_out, multiplexer_5_out, not_1_out, not_2_out, not_3_out;

  Multiplexer #(.width(16), .enable("false")) multiplexer_1 (
    .in0(x), .in1({16{1'b0}}), .out(multiplexer_1_out), .sel(zx));
  Multiplexer #(.width(16), .enable("false")) multiplexer_2 (
    .in0(y), .in1({16{1'b0}}), .out(multiplexer_2_out), .sel(zy));
  assign not_1_out = ~multiplexer_1_out;  // NOT_Gate not_1, 16 bits wide
  assign not_2_out = ~multiplexer_2_out;  // NOT_Gate not_2, 16 bits wide
  Multiplexer #(.width(16), .enable("false")) multiplexer_3 (
    .in0(x), .in1(not_1_out), .out(multiplexer_3_out), .sel(nx));
  Multiplexer #(.width(16), .enable("false")) multiplexer_4 (
    .in0(y), .in1(not_2_out), .out(multiplexer_4_out), .sel(ny));
  assign and_1_out = multiplexer_3_out & multiplexer_4_out;  // AND_Gate and_1, 16 bits wide
  Add16 add16_1 (.B(multiplexer_4_out), .A(multiplexer_3_out), .Sum(add16_1_sum));  // open: Carry
  Multiplexer #(.width(16), .enable("false")) multiplexer_5 (
    .in0(and_1_out), .in1(add16_1_sum), .out(multiplexer_5_out), .sel(f));
  assign not_3_out = ~multiplexer_5_out;  // NOT_Gate not_3, 16 bits wide
  Multiplexer #(.width(16), .enable("false")) multiplexer_6 (
    .in0(not_3_out), .in1(multiplexer_5_out), .out(out), .sel(no));
  Or16Way or16way_1 (.A(out), .Or(or16way_1_or));
  not not_4 (zr, or16way_1_or);
  assign {ng, and_2_out} = out & {16{1'b1}};  // AND_Gate and_2, 16 bits wide
endmodule

module Add4 (
  input  [3:0] A,
  input  [3:0] B,
  input  C,
  output [3:0] Sum,
  output Carry
);

  wire fa_2_carry, fa_3_carry, fa_4_carry;

  FA fa_1 (.a(fa_4_carry), .b(B[3]), .c(A[3]), .sum(Sum[3]), .carry(Carry));
  FA fa_2 (.a(C), .b(B[0]), .c(A[0]), .sum(Sum[0]), .carry(fa_2_carry));
  FA fa_3 (.a(fa_2_carry), .b(B[1]), .c(A[1]), .sum(Sum[1]), .carry(fa_3_carry));
  FA fa_4 (.a(fa_3_carry), .b(B[2]), .c(A[2]), .sum(Sum[2]), .carry(fa_4_carry));
endmodule

module Reg16 (
  input  [15:0] in_1,
  input  in_2,
  input  in_3,
  output [15:0] out_4
);

  wire clock_1_out;

  Clock clock_1 (.out(clock_1_out));
  Register #(.width(16)) register_1 (.D(in_1), .en(in_2), .clk(clock_1_out), .Q(out_4), .clr(in_3));
endmodule
